# Fritzing sketch OnAir (saved by Fritzing 0.9.10b)
breadboards: 1

parts:
  Mod1 = Amica NodeMCU DEVKIT 1.0
  RGB_SMD_LED1 = SMD RGB LED (WS2812) [package=5050]
  RGB_SMD_LED2 = SMD RGB LED (WS2812) [package=5050]

nets:
  N1: Mod1.pin1, Mod1.pin_10, Mod1.pin_26
  VSS: Mod1.pin2, Mod1.pin_9, Mod1.pin_25, Mod1.pin_29, RGB_SMD_LED1.VSS, RGB_SMD_LED2.VSS
  N2: Mod1.pin_13, RGB_SMD_LED2.DIn
  N3: Mod1.pin_14, RGB_SMD_LED1.DIn
  VDD: RGB_SMD_LED1.VDD, RGB_SMD_LED2.VDD

notes:
  Tady používám piny D1 a D2 pro řízení těch dvou kruhů. Budu muset ještě zjistit, které piny jsou vhodný použít.
  Tenhle modul WS2812 představuje jeden ten kruh, který má vývody
  GND - zem
  5V - napájení
  DI - datový pin
  DO - patrně taky datový pin, aby se daly řadit za sebe
  Označení vstupů tady tomu neodpovídá, ale lepší součástku jsem tady nenašel.
  Napájení 3.3V
  Dávám přednost napájet mikrokontroler z těch pinů 3v3 spíš než přes USB mini. Další kabel by to zapojení komplikoval.
  Napájení 5V
